// Logisim project 1751023.circ as structural Verilog: 1 circuit, main circuit main
module main (
  input  in_1,
  input  in_2,
  input  in_3,
  input  in_4,
  input  in_5,
  input  in_6,
  output out_7,
  output out_8,
  output out_9,
  output out_10
);

  wire and_1_out, and_2_out, and_3_out, and_4_out, and_5_out, and_6_out, and_7_out, and_8_out, clock_1_out,
       not_1_out, or_1_out, or_2_out, or_3_out, or_4_out;

  or or_1 (or_1_out, and_1_out, and_2_out);
  and and_1 (and_1_out, in_1, not_1_out);
  not not_1 (not_1_out, in_2);
  D_Flip_Flop d_ff_1 (.clk(clock_1_out), .D(or_1_out), .Q(out_7));  // open: Qn, preset, en, reset
  and and_2 (and_2_out, in_2, in_3);
  or or_2 (or_2_out, and_3_out, and_4_out);
  and and_3 (and_3_out, out_7, not_1_out);
  and and_4 (and_4_out, in_2, in_4);
  D_Flip_Flop d_ff_2 (.clk(clock_1_out), .D(or_2_out), .Q(out_8));  // open: Qn, preset, en, reset
  or or_3 (or_3_out, and_5_out, and_6_out);
  and and_5 (and_5_out, out_8, not_1_out);
  D_Flip_Flop d_ff_3 (.clk(clock_1_out), .D(or_3_out), .Q(out_9));  // open: Qn, preset, en, reset
  and and_6 (and_6_out, in_2, in_5);
  or or_4 (or_4_out, and_7_out, and_8_out);
  and and_7 (and_7_out, out_9, not_1_out);
  and and_8 (and_8_out, in_2, in_6);
  D_Flip_Flop d_ff_4 (.clk(clock_1_out), .D(or_4_out), .Q(out_10));  // open: Qn, preset, en, reset
  Clock clock_1 (.out(clock_1_out));
endmodule
