// Logisim project 7-segment.circ as structural Verilog: 1 circuit, main circuit main
module main (
  input  in_1,
  input  in_2,
  input  in_3,
  input  in_4
);

  wire and_1_out, and_2_out, and_3_out, and_4_out, and_5_out, and_6_out, and_7_out, and_8_out, and_9_out,
       not_1_out, not_2_out, not_3_out, or_1_out, or_2_out, or_3_out, or_4_out, or_5_out, or_6_out, or_7_out;

  not not_1 (not_1_out, in_1);
  not not_2 (not_2_out, in_2);
  not not_3 (not_3_out, in_3);
  and and_1 (and_1_out, in_1, not_2_out, in_3);
  and and_2 (and_2_out, not_1_out, in_2);
  and and_3 (and_3_out, in_2, not_3_out);
  and and_4 (and_4_out, not_1_out, not_3_out);
  and and_5 (and_5_out, in_3, not_2_out);
  and and_6 (and_6_out, in_1, in_2);
  and and_7 (and_7_out, not_1_out, not_2_out);
  and and_8 (and_8_out, not_1_out, in_3);
  and and_9 (and_9_out, in_3, in_1);
  or or_1 (or_1_out, and_1_out, and_2_out, and_3_out, and_4_out, in_4);
  or or_2 (or_2_out, and_4_out, and_2_out);
  or or_3 (or_3_out, and_2_out, in_4, and_3_out, and_5_out);
  or or_4 (or_4_out, in_1, not_2_out, in_3);
  or or_5 (or_5_out, not_3_out, and_6_out, and_7_out);
  _7_Segment_Display u_7_segment_display_1 (
    .g(or_1_out), .f(or_2_out), .a(or_3_out), .b(or_4_out), .e(or_5_out), .d(or_6_out), .c(or_7_out));  // open: dp
  or or_6 (or_6_out, and_8_out, in_4, and_5_out, and_7_out);
  or or_7 (or_7_out, in_2, and_4_out, in_4, and_9_out);
endmodule
