// Logisim project D, T FLip FLops.circ as structural Verilog: 1 circuit, main circuit main
module main (
  input  in_1,
  output out_2,
  output out_3,
  output out_4,
  output out_5,
  output out_6,
  output out_7
);

  wire clock_1_out, clock_2_out, d_ff_1_qn, d_ff_2_qn, d_ff_3_qn, t_ff_1_qn, t_ff_2_qn;

  Clock clock_1 (.out(clock_1_out));
  Clock clock_2 (.out(clock_2_out));
  D_Flip_Flop d_ff_1 (.clk(clock_1_out), .D(d_ff_1_qn), .Q(out_2), .Qn(d_ff_1_qn));  // open: preset, en, reset
  T_Flip_Flop t_ff_1 (.clk(clock_2_out), .T(in_1), .Q(out_5), .Qn(t_ff_1_qn));  // open: preset, reset, en
  D_Flip_Flop d_ff_2 (.clk(d_ff_1_qn), .D(d_ff_2_qn), .Q(out_3), .Qn(d_ff_2_qn));  // open: preset, en, reset
  T_Flip_Flop t_ff_2 (.clk(t_ff_1_qn), .T(in_1), .Q(out_6), .Qn(t_ff_2_qn));  // open: preset, reset, en
  D_Flip_Flop d_ff_3 (.clk(d_ff_2_qn), .D(d_ff_3_qn), .Q(out_4), .Qn(d_ff_3_qn));  // open: preset, en, reset
  T_Flip_Flop t_ff_3 (.clk(t_ff_2_qn), .T(in_1), .Q(out_7));  // open: Qn, preset, reset, en
endmodule
