// Logisim project Multiplication.circ as structural Verilog: 1 circuit, main circuit main
module main (
  input  in_1,
  input  [7:0] in_2,
  input  [7:0] in_3,
  input  in_4,
  input  in_5,
  input  in_6
);

  wire adder_1_cout, and_1_out, clock_1_out, not_1_out, not_2_out, shift_register_1_out,
       shift_register_2_out, shift_register_3_out, t_ff_1_q;
  wire [7:0] adder_1_out, multiplexer_1_out, shift_register_2_q7;

  Clock clock_1 (.out(clock_1_out));
  not not_1 (not_1_out, shift_register_1_out);
  Shift_Register shift_register_1 (
    .shift(in_5), .clk(in_6), .out(shift_register_1_out));  // open: in, load, clr, d0, q0, d1, q1, d2, q2, d3, q3, d4, q4, d5, q5, d6, q6, d7, q7
  T_Flip_Flop t_ff_1 (.T(in_4), .Q(t_ff_1_q));  // open: clk, Qn, preset, reset, en
  and and_1 (and_1_out, clock_1_out, not_1_out);
  not not_2 (not_2_out, t_ff_1_q);
  Shift_Register shift_register_2 (
    .shift(not_2_out), .in(adder_1_cout), .clk(and_1_out), .out(shift_register_2_out), .load(t_ff_1_q),
    .d0(adder_1_out[7]), .q0(shift_register_2_q7[7]), .d1(adder_1_out[6]), .q1(shift_register_2_q7[6]),
    .d2(adder_1_out[5]), .q2(shift_register_2_q7[5]), .d3(adder_1_out[4]), .q3(shift_register_2_q7[4]),
    .d4(adder_1_out[3]), .q4(shift_register_2_q7[3]), .d5(adder_1_out[2]), .q5(shift_register_2_q7[2]),
    .d6(adder_1_out[1]), .q6(shift_register_2_q7[1]), .d7(adder_1_out[0]), .q7(shift_register_2_q7[0]));  // open: clr
  Shift_Register shift_register_3 (
    .shift(not_2_out), .in(shift_register_2_out), .clk(and_1_out), .out(shift_register_3_out));  // open: load, clr, d0, q0, d1, q1, d2, q2, d3, q3, d4, q4, d5, q5, d6, q6, d7, q7
  Adder adder_1 (.a(shift_register_2_q7), .b(multiplexer_1_out), .out(adder_1_out), .cin(in_1), .cout(adder_1_cout));
  Multiplexer #(.width(8)) multiplexer_1 (
    .in0(in_2), .in1(in_3), .out(multiplexer_1_out), .sel(shift_register_3_out));  // open: en
endmodule
